# Fritzing sketch 1Wire 12V Eingang (saved by Fritzing 1.0.1rc)
breadboards: 1

parts:
  VCC1 = Battery block 9V
  VM1 = Multimeter (DC Voltage)
  VCC2 = Battery  # not connected
  R1 = Resistor [tolerance=±5% resistance=2.2k package="1206 [SMD]"]
  VM2 = Multimeter (Ohmmeter)
  VM3 = Multimeter (DC Voltage)
  Q2 = NPN-Transistor [package="TO92 [THT]"]
  S1 = Toggle Switch [package=THT]
  J8 = male pin header, 2 pins [form="♂ (male)"]

nets:
  N1: VCC1.-, VM1.COM_Probe, VM2.COM_Probe, VM3.COM_Probe, Q2.E
  N2: VCC1.+, S1.COM
  N3: VM1.V_Probe, R1.Pin_0, R1.Pin_1, Q2.B, S1.L2, J8.pin1, J8.pin2
  N4: VM2.V_Probe, VM3.V_Probe, Q2.C
