# Fritzing sketch 1Wire Injektor (saved by Fritzing 1.0.1rc)
stripboards: 1

parts:
  U1 = Mini-360 DC-DC Buck converter [package=THT]
  J3 = screw terminal, 8 pins
  J6 = Camdenboss CTB0158-2 [part_number=CTB0158-2 package=THT]
  J7 = screw terminal, 8 pins

nets:
  N1: U1.IN-, J3.pin1, J6.pin1, J7.pin1
  N2: U1.IN+, J3.pin2, J6.pin2, J7.pin2
  N3: U1.OUT+, J3.pin7, J7.pin7
  N4: U1.OUT-, J3.pin8, J7.pin8
  N5: J3.pin3, J7.pin5
  N6: J3.pin4, J7.pin6
  N7: J3.pin5, J7.pin3
  N8: J3.pin6, J7.pin4

notes:
  12V GND
  5V GND
  1W GND =>
  5V +
  1W GND <=
  12V +
  1W Dat =>
  1W Dat <=

custom parts:
  Mini-360 DC-DC Buck converter: Mini-360 DC-DC Buck converter. Tiny buck step down voltage converter, input voltage 4.75 to 23V output 1 to 17V adjustable. Available from ebay and the like.
