# Fritzing sketch 1Wire Netzteil (saved by Fritzing 1.0.1rc)
stripboards: 1

parts:
  U1 = Mini-360 DC-DC Buck converter [package=THT]
  J6 = Camdenboss CTB0158-2 [part_number=CTB0158-2 package=THT]
  J7 = Camdenboss CTB0158-2 [part_number=CTB0158-2 package=THT]
  J8 = Camdenboss CTB0158-2 [part_number=CTB0158-2 package=THT]

nets:
  N1: U1.IN-, J8.pin2
  N2: U1.IN+, J6.pin2, J8.pin1
  N3: U1.OUT+, J7.pin1
  N4: U1.OUT-, J6.pin1

notes:
  GND
  12V +
  5V +

custom parts:
  Mini-360 DC-DC Buck converter: Mini-360 DC-DC Buck converter. Tiny buck step down voltage converter, input voltage 4.75 to 23V output 1 to 17V adjustable. Available from ebay and the like.
