# Fritzing sketch 1Wire Unterverteiler USB-C (saved by Fritzing 1.0.1rc)
stripboards: 1

parts:
  A1 = RJ45 Breakout 1-Wire
  A2 = RJ45 Breakout 1-Wire
  A3 = RJ45 Breakout 1-Wire
  Bauteil1 = Adafruit USB Type C Breakout MRA  # not connected
  Bauteil2 = Adafruit USB Type C Breakout MRA  # not connected
  Bauteil3 = Adafruit USB Type C Breakout MRA  # not connected

nets:
  N1: A1.5V_GND, A2.5V_GND, A3.5V_GND
  N2: A1.5V_+, A2.5V_+, A3.5V_+
  N3: A1.1W_GND_Raus, A3.1W_GND_Raus
  N4: A1.1W_DAT_Rein, A2.1W_DAT_Rein
  N5: A1.1W_GND_Rein, A2.1W_GND_Rein
  N6: A1.1W_DAT_Raus, A3.1W_DAT_Raus
  N7: A1.12V_+, A2.12V_+, A3.12V_+
  N8: A1.12V_GND, A2.12V_GND, A3.12V_GND
  N9: A2.1W_GND_Raus, A3.1W_GND_Rein
  N10: A2.1W_DAT_Raus, A3.1W_DAT_Rein

notes:
  12V GND
  12V +
  1W Dat <=
  1W GND =>
  1W Dat =>
  1W GND <=
  5V GND
  5V +
  1
  2
  3

custom parts:
  Adafruit USB Type C Breakout MRA: breakout board for USB Type C socket 6 Pin
