# Fritzing sketch 1Wire Verteiler (saved by Fritzing 1.0.1rc)
stripboards: 1

parts:
  U1 = Mini-360 DC-DC Buck converter [package=THT]
  J1 = screw terminal, 8 pins
  J2 = screw terminal, 8 pins
  J3 = screw terminal, 8 pins
  J4 = screw terminal, 8 pins
  J5 = Camdenboss CTB0158-2 [part_number=CTB0158-2 package=THT]

nets:
  N1: U1.IN-, J1.pin1, J2.pin1, J3.pin1, J4.pin1, J5.pin1
  N2: U1.IN+, J1.pin2, J2.pin2, J3.pin2, J4.pin2, J5.pin2
  N3: U1.OUT+, J1.pin7, J2.pin7, J3.pin7, J4.pin7
  N4: U1.OUT-, J1.pin8, J2.pin8, J3.pin8, J4.pin8
  N5: J1.pin4, J2.pin4
  N6: J1.pin5, J2.pin5
  N7: J2.pin3, J3.pin5
  N8: J2.pin6, J3.pin4
  N9: J3.pin3, J4.pin3
  N10: J3.pin6, J4.pin6

notes:
  12V GND
  12V +
  1W Dat <=
  1W GND =>
  1W Dat =>
  1W GND <=
  5V GND
  5V +
  1
  2
  3
  4

custom parts:
  Mini-360 DC-DC Buck converter: Mini-360 DC-DC Buck converter. Tiny buck step down voltage converter, input voltage 4.75 to 23V output 1 to 17V adjustable. Available from ebay and the like.
