# Fritzing sketch 1WireTemp - Streifenplatine (saved by Fritzing 1.0.1rc)
stripboards: 1

parts:
  TFT1 = 1.44" SPI TFT Graphics Display 128x128 - MR 8pin [package=THT]
  R1 = Resistor [tolerance=±5% power=0.25W resistance=4.7k package=THT]
  DS1 = DS18B20 1-Wire Temperature Sensor [part_number=DS18B20]
  Sensor1 = TTP223B Capacitive Touch Sensor Module
  M1 = Arduino NANO RP2040 CONNECT with headers
  J2 = female pin header, 2 pins [form="♀ (female)"]
  J4 = screw terminal, 3 pins
  J6 = female pin header, 8 pins [form="♀ (female)"]
  J7 = female pin header, 15 pins [form="♀ (female)"]
  J8 = female pin header, 15 pins [form="♀ (female)"]
  J9 = screw terminal, 3 pins

nets:
  VDD: TFT1.pin1, R1.Pin_1, DS1.VDD, Sensor1.VCC, M1.D15, M1.VIN, J2.pin2, J4.pin2, J6.pin1, J7.pin5, J7.pin15, J9.pin3
  GND: TFT1.pin2, DS1.GND, Sensor1.GND, M1.GND-4, M1.D17, M1.D27, M1.RESET-28, M1.GND-29, J4.pin1, J6.pin2, J7.pin7, J7.pin11, J7.pin13, J7.pin14, J8.pin12, J9.pin1
  N1: TFT1.pin3, M1.D7, J6.pin3, J8.pin6
  N2: TFT1.pin4, M1.D6, J6.pin4, J8.pin7
  N3: TFT1.pin5, M1.D5, J6.pin5, J8.pin8
  N4: TFT1.pin6, M1.D11, J6.pin6, J8.pin2
  N5: TFT1.pin7, M1.D13, J6.pin7, J7.pin1
  N6: TFT1.pin8, M1.D2, M1.D3, J6.pin8, J8.pin10, J8.pin11
  N7: R1.Pin_0, DS1.DQ, M1.D10, J2.pin1, J4.pin3, J8.pin3
  N8: Sensor1.SIG, M1.D16, M1.D18, J7.pin6, J7.pin8, J9.pin2
  N9: M1.TX, J8.pin15
  N10: M1.RX, J8.pin14
  N11: M1.RESET-3, J8.pin13
  N12: M1.D4, J8.pin9
  N13: M1.D8, J8.pin5
  N14: M1.D9, J8.pin4
  N15: M1.D12, J8.pin1
  N16: M1.+3V3, J7.pin2
  N17: M1.AREF, J7.pin3
  N18: M1.D14, J7.pin4
  N19: M1.D19, J7.pin9
  N20: M1.D20, J7.pin10
  N21: M1.+5V, J7.pin12

custom parts:
  TTP223B Capacitive Touch Sensor Module: The TTP223B capacitive touch sensor module uses the TTP223B IC. The appropriate voltage is approximately 2 to 5.5 volts.
