# Fritzing sketch 1WireTemp (saved by Fritzing 1.0.1rc)
circuit board: 10.1317cm x 10.7978cm
breadboards: 1

parts:
  TFT1 = 1.44" SPI TFT Graphics Display 128x128 - MR 8pin [package=THT]
  Sensor1 = TTP223B Capacitive Touch Sensor Module
  M6 = Arduino Nano 33 IOT-tht

nets:
  N1: TFT1.pin1, Sensor1.GND, M6.pin_15
  N2: TFT1.pin2, M6.pin_14, M6.pin_19
  N3: TFT1.pin3, M6.pin_25
  N4: TFT1.pin4, M6.pin_24
  N5: TFT1.pin5, M6.pin_23
  N6: TFT1.pin6, M6.pin_29
  N7: TFT1.pin7, M6.pin_1
  N8: TFT1.pin8, M6.pin_21
  N9: Sensor1.VCC, M6.pin_12
  N10: Sensor1.SIG, M6.pin_8
  N11: M6.pin_13, M6.pin_18

custom parts:
  TTP223B Capacitive Touch Sensor Module: The TTP223B capacitive touch sensor module uses the TTP223B IC. The appropriate voltage is approximately 2 to 5.5 volts.
  Arduino Nano 33 IOT-tht: The Arduino Nano 33 IoT is the easiest and cheapest point of entry to enhance existing devices (and creating new ones) to be part of the IoT and designing pico-network applications. Whether you are looking at building a sensor network connected to your office or home router, or if you want to create a BLE device sending data to a cellphone, the Nano 33 IoT is your one-stop-solution for many of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
