# Fritzing sketch DS2438 Sondenadapter (saved by Fritzing 1.0.1rc)
stripboards: 1

parts:
  VR2 = DS2438 [part_number=DS2438 package=SO]
  J5 = Camdenboss CTB0158-3 [part_number=CTB0158-3 package=THT]
  A1 = SparkFun RJ45 Breakout v11

nets:
  N1: VR2.pin_1, J5.pin3, A1.Pin_1, A1.Pin_3, A1.Pin_5, A1.Pin_8
  N2: VR2.pin_3, VR2.pin_4, J5.pin2
  N3: VR2.pin_5, A1.Pin_2
  N4: VR2.pin_8, A1.Pin_4, A1.Pin_6
  N5: J5.pin1, A1.Pin_7

notes:
  6 - 1W DAT =>
  5 - 1W GND <=
  7 - +12V
  2 - +5V
  0-2V
  GND
  +12V
  8 - GND 12V
  1 - 5V GND
  3 - 1W GND =>
  4 - 1W DAT <=

custom parts:
  DS2438: 1-Wire DS2438 Smart Battery Monitor
  SparkFun RJ45 Breakout v11: SparkFun RJ45 Breakout v11 breakout board.
