# Fritzing sketch Voltmeter Test (saved by Fritzing 1.0.1rc)
breadboards: 1

parts:
  VM1 = Multimeter (DC Voltage)
  R1 = Rotary Potentiometer (Small) [maximum_resistance=10kΩ knob_status=99% power=0.5W package=THT]
  BAT1 = Battery Holders [package=battery-aaa]
  BAT2 = Battery Holders [package=battery-aaa]
  BAT3 = Battery Holders [package=battery-aaa]
  R2 = Resistor [tolerance=±5% power=0.25W resistance=4.7k package=THT]
  AM1 = Multimeter (DC Voltage)
  R3 = Resistor [tolerance=±5% power=0.25W resistance=2.2k package=THT]
  AM2 = Multimeter (DC Current)

nets:
  N1: VM1.COM_Probe, R1.leg2, AM1.COM_Probe, AM2.A_Probe
  N2: VM1.V_Probe, R1.wiper
  N3: R1.leg1, R2.Pin_1
  N4: BAT1.-, AM2.COM_Probe
  N5: BAT1.+, BAT2.-
  N6: BAT2.+, BAT3.-
  N7: BAT3.+, AM1.V_Probe, R3.Pin_0
  N8: R2.Pin_0, R3.Pin_1
